# Fritzing sketch lolin32_mqtt_bme280 (saved by Fritzing 0.9.3b)
breadboards: 1

parts:
  U1 = lolin
  Bauteil1 = BME280 Breakout
  U2 = LIPO-2000mAh [package=lipo-2000]

nets:
  N1: U1.connector16, U2.-
  N2: U1.connector17, U2.+
  N3: U1.connector20, Bauteil1.GND
  N4: U1.connector28, Bauteil1.SCK/SCL
  N5: U1.connector32, Bauteil1.SDI/SDA
  N6: U1.connector34, Bauteil1.3.3V
